# Fritzing sketch circuit_diagram (saved by Fritzing 0.9.5d)
perfboards: 1

parts:
  esp1 = ESP32 DevKitc V4  # not connected
  U1 = LIPO-1000mAh [package=lipo-1000]
  L298N1 = L298N DC motor driver
  A1 = DFR0379
  F1 = FUSE [package=fuse_5mm]
  S1 = Square Pushbutton
  J1 = female pin header, 19 pins [form="♀ (female)"]  # not connected
  J2 = female pin header, 19 pins [form="♀ (female)"]
  DC_Mot_Enc1 = DC Motor with two-phase hall-encoder [part_number=VT-E-G25A-06-177E]
  DC_Mot_Enc2 = DC Motor with two-phase hall-encoder [part_number=VT-E-G25A-06-177E]
  J1_2 = female pin header, 2 pins [form="♀ (female)"]
  J4 = female pin header, 2 pins [form="♀ (female)"]
  J5 = female pin header, 2 pins [form="♀ (female)"]
  J3 = male pin header, 2 pins [form="♂ (male)"]
  J6 = female pin header, 2 pins [form="♀ (female)"]
  J7 = female alternating pin header, 2 pins [form="♀ (female)"]
  J8 = male pin header, 2 pins [form="♂ (male)"]
  J3_2 = male pin header, 8 pins [form="♂ (male)"]

nets:
  N1: U1.+, J3.pin1
  N2: U1.-, L298N1.GND, J6.pin1
  N3: L298N1.OUT1, DC_Mot_Enc2.pin1
  N4: L298N1.OUT2, DC_Mot_Enc2.pin2
  N5: L298N1.OUT3, DC_Mot_Enc1.pin1
  N6: L298N1.OUT4, DC_Mot_Enc1.pin2
  N7: L298N1.12V, S1.leg0, J6.pin2
  N8: L298N1.ENA, J2.pin11, J3_2.pin6
  N9: L298N1.ENB, J2.pin16, J3_2.pin1
  N10: L298N1.IN1, J2.pin12, J3_2.pin5
  N11: L298N1.IN2, J2.pin13, J3_2.pin4
  N12: L298N1.IN3, J2.pin14, J3_2.pin3
  N13: L298N1.IN4, J2.pin15, J3_2.pin2
  N14: A1.Pin_2, J1_2.pin2
  N15: A1.Pin_3, A1.Pin_5, A1.Pin_6, J1_2.pin1, J7.pin1
  N16: A1.Pin_7, J7.pin2
  N17: F1.1, S1.leg1
  N18: J2.pin2, DC_Mot_Enc1.pin3, J8.pin2
  N19: J2.pin3, DC_Mot_Enc1.pin4, J8.pin1
  N20: J2.pin9, DC_Mot_Enc2.pin3, J3_2.pin8
  N21: J2.pin10, DC_Mot_Enc2.pin4, J3_2.pin7
  N22: DC_Mot_Enc1.pin5, J4.pin1
  N23: DC_Mot_Enc1.pin6, J4.pin2
  N24: DC_Mot_Enc2.pin5, J5.pin1
  N25: DC_Mot_Enc2.pin6, J5.pin2

custom parts:
  ESP32 DevKitc V4: ESP32-DevKitC board with ESP32-WROOM-32 module. ESP32-DevKitC V4 is a small-sized ESP32-based development board produced by Espressif. Most of the pins on the ESP module are broken out to the pin headers on the board. The pins D0, D1, D2, D3, CMD and CLK are used internally for communication between ESP32 and SPI flash memory. They are grouped on both sides near the USB connector. Avoid using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
  L298N DC motor driver: 2x DC motor driver with 78M05 positive voltage regulator (7..35 V) L298N: max 46 V, 2 A Set 5 V Enable jumper to enable 5 V regultor (needed for the L298N) and +5 V output at screw terminal or supply external +5 V at screw terminal Set ENA and/or ENB to +5 V to enable motor permanently or supply ENA and/or ENB with PWM signal IN1 and IN2 set rotation directory for motor A (OUT1/OUT2) IN2 and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
  DFR0379: 20W Adjustable DC-DC Buck Converter with Digital Display.
